// Logisim project oisc.circ as structural Verilog: 1 circuit, main circuit main
module main (
);

  wire buffer_1_out, CLK, demultiplexer_4_out0, demultiplexer_4_out1, MICRO_RST, not_1_out, not_2_out,
       OE_ALU, OE_GENERAL, OE_HADDR, OE_HPC, OE_IO, OE_LADDR, OE_LPC, OE_MEM, OE_RAM, OE_ROM, OE_SCRATCH0,
       OE_SCRATCH1, OE_X, OE_Y, SUFFIX_SELECT, WE_GENERAL, WE_HADDR, WE_HPC, WE_IO, WE_LADDR, WE_LPC, WE_MEM,
       WE_RAM, WE_SCRATCH0, WE_SCRATCH1, WE_X, WE_Y, Z_DETECT;
  wire [2:0] LADDR_q, OE_SELECT, SUFFIX_BITS, WE_SELECT;
  wire [4:0] MICRO_ADDR;
  wire [7:0] controlled_buffer_8_out, DATA, HPC_2_q, HPC_q, LPC_2_q, LPC_q, NOR_out, X_q, Y_q;
  wire [15:0] ADDRESS;

  Register #(.trigger("high")) X (.D(DATA), .en(1'b1), .Q(X_q), .clk(WE_X));  // open: clr
  Register #(.trigger("high")) Y (.D(DATA), .en(1'b1), .Q(Y_q), .clk(WE_Y));  // open: clr
  Register #(.trigger("high")) HPC (.D(DATA), .Q(HPC_q), .clk(WE_HPC));  // open: en, clr
  assign DATA = OE_HPC ? HPC_q : 8'bz;  // Controlled_Buffer controlled_buffer_1
  Register #(.trigger("high")) HPC_2 (.D(DATA), .Q(HPC_2_q), .clk(WE_SCRATCH1));  // open: en, clr
  assign DATA = OE_SCRATCH1 ? HPC_2_q : 8'bz;  // Controlled_Buffer controlled_buffer_2
  Register #(.trigger("high")) HADDR (.D(DATA), .Q(ADDRESS[15:8]), .clk(WE_HADDR));  // open: en, clr
  assign DATA = OE_HADDR ? ADDRESS[15:8] : 8'bz;  // Controlled_Buffer controlled_buffer_3
  assign NOR_out = ~(X_q | Y_q);  // NOR_Gate NOR, 8 bits wide
  assign DATA = OE_ALU ? NOR_out : 8'bz;  // Controlled_Buffer controlled_buffer_4
  assign DATA = OE_LPC ? LPC_q : 8'bz;  // Controlled_Buffer controlled_buffer_5
  Register #(.trigger("high")) LPC (.D(DATA), .Q(LPC_q), .clk(WE_LPC));  // open: en, clr
  Register #(.trigger("high")) LPC_2 (.D(DATA), .Q(LPC_2_q), .clk(WE_SCRATCH0));  // open: en, clr
  assign DATA = OE_SCRATCH0 ? LPC_2_q : 8'bz;  // Controlled_Buffer controlled_buffer_6
  Register #(.trigger("high")) LADDR (.D(DATA), .Q({ADDRESS[7:3], LADDR_q}), .clk(WE_LADDR));  // open: en, clr
  assign DATA = OE_LADDR ? {ADDRESS[7:3], LADDR_q} : 8'bz;  // Controlled_Buffer controlled_buffer_7
  not not_1 (not_1_out, WE_RAM);
  Multiplexer #(.width(3), .enable("false")) multiplexer_1 (
    .in0(LADDR_q), .in1(SUFFIX_BITS), .out(ADDRESS[2:0]), .sel(SUFFIX_SELECT));
  assign controlled_buffer_8_out = WE_RAM ? DATA : 8'bz;  // Controlled_Buffer controlled_buffer_8
  RAM #(.addrWidth(16), .bus("asynch")) ram_1 (
    .addr(ADDRESS), .data(controlled_buffer_8_out), .ld(not_1_out));  // open: sel, clr
  assign DATA = OE_RAM ? controlled_buffer_8_out : 8'bz;  // Controlled_Buffer controlled_buffer_9
  nor Z (Z_DETECT, NOR_out[0], NOR_out[1], NOR_out[2], NOR_out[3], NOR_out[4], NOR_out[5], NOR_out[6], NOR_out[7]);
  // Probe on DATA
  // Probe on ADDRESS
  Counter #(.width(5), .max('h1f)) counter_1 (
    .Q(MICRO_ADDR), .clk(CLK), .clr(MICRO_RST));  // open: load, D, count, carry
  Clock CLK1 (.out(CLK));
  ROM #(.addrWidth(16)) rom_1 (.addr(ADDRESS), .data(DATA), .sel(OE_ROM));
  Demultiplexer #(.select(3)) demultiplexer_1 (
    .out0(WE_X), .out1(WE_Y), .out2(WE_HPC), .out3(WE_LPC), .out4(WE_HADDR), .out5(WE_LADDR),
    .out6(WE_SCRATCH1), .out7(WE_SCRATCH0), .in(WE_GENERAL), .sel(WE_SELECT), .en(1'b1));
  buf buffer_1 (buffer_1_out, OE_GENERAL);
  Demultiplexer #(.select(3)) demultiplexer_2 (
    .out0(OE_X), .out1(OE_Y), .out2(OE_HPC), .out3(OE_LPC), .out4(OE_HADDR), .out5(OE_LADDR),
    .out6(OE_SCRATCH1), .out7(OE_SCRATCH0), .in(buffer_1_out), .sel(OE_SELECT), .en(1'b1));
  not not_2 (not_2_out, CLK);
  Demultiplexer #(.select(2), .enable("false")) demultiplexer_3 (
    .out2(WE_RAM), .out3(WE_IO), .in(WE_MEM), .sel(ADDRESS[15:14]));  // open: out0, out1
  Demultiplexer #(.select(2), .enable("false")) demultiplexer_4 (
    .out0(demultiplexer_4_out0), .out1(demultiplexer_4_out1), .out2(OE_RAM), .out3(OE_IO), .in(OE_MEM),
    .sel(ADDRESS[15:14]));
  ROM #(.addrWidth(6), .dataWidth(16)) rom_2 (
    .addr({Z_DETECT, MICRO_ADDR}),
    .data({OE_GENERAL, OE_SELECT, WE_GENERAL, WE_SELECT, SUFFIX_SELECT, SUFFIX_BITS, OE_ALU, WE_MEM, OE_MEM, MICRO_RST}),
    .sel(not_2_out));
  Pull_Resistor pull_resistor_1 (.node({OE_GENERAL, OE_SELECT, WE_GENERAL, WE_SELECT, SUFFIX_SELECT, SUFFIX_BITS, OE_ALU, WE_MEM, OE_MEM, MICRO_RST}));
  or or_1 (OE_ROM, demultiplexer_4_out0, demultiplexer_4_out1);

  // Notes on the sheet:
  //   ALU
  //   RAM
  //   PROGRAM ROM
  //   MICROCODE
  //   contents of rom_2 (hex, n*v repeats v):
  //   ac00 bd00 ea2 fb2 ec00 fd00 902 ac00 bd00 e82 f92 ec00 fd00 802 c ac00 bd00 ac2 bd2 1 12*0 ac00 bd00
  //   ea2 fb2 ec00 fd00 902 ac00 bd00 e82 f92 ec00 fd00 802 c ac00 bd00 ae2 bf2 1
endmodule
